// Logisim project UpDownCounterTo7Segment.circ as structural Verilog: 1 circuit, main circuit main
module main (
  input  _1_for_up_Counter_0_for_down_counter,
  input  Clock,
  output a,
  output b,
  output c,
  output d,
  output e,
  output f,
  output g
);

  wire j_k_ff_1_q, j_k_ff_1_qn, j_k_ff_2_q, j_k_ff_2_qn, j_k_ff_3_q, nand_1_out, nand_2_out, nand_3_out,
       nand_4_out, nand_5_out, nand_6_out, not_1_out;

  not not_1 (not_1_out, _1_for_up_Counter_0_for_down_counter);
  J_K_Flip_Flop #(.trigger("falling")) j_k_ff_1 (
    .J(1'b1), .clk(Clock), .K(1'b1), .Q(j_k_ff_1_q), .Qn(j_k_ff_1_qn));  // open: preset, en, reset
  nand nand_1 (nand_1_out, _1_for_up_Counter_0_for_down_counter, j_k_ff_1_q);
  nand nand_2 (nand_2_out, j_k_ff_1_qn, not_1_out);
  nand nand_3 (nand_3_out, nand_1_out, nand_2_out);
  J_K_Flip_Flop #(.trigger("falling")) j_k_ff_2 (
    .J(1'b1), .clk(nand_3_out), .K(1'b1), .Q(j_k_ff_2_q), .Qn(j_k_ff_2_qn));  // open: preset, en, reset
  nand nand_4 (nand_4_out, _1_for_up_Counter_0_for_down_counter, j_k_ff_2_q);
  nand nand_5 (nand_5_out, j_k_ff_2_qn, not_1_out);
  nand nand_6 (nand_6_out, nand_4_out, nand_5_out);
  J_K_Flip_Flop #(.trigger("falling")) j_k_ff_3 (
    .J(1'b1), .clk(nand_6_out), .K(1'b1), .Q(j_k_ff_3_q));  // open: Qn, preset, en, reset
  // _7_segment_display_driver 7_segment_display_driver_1: pin names not known; wires that end beside it: 1'b0, j_k_ff_3_q, j_k_ff_2_q, j_k_ff_1_q, a, b, c, d, e, f, g
endmodule
